// Logisim project factor.circ as structural Verilog: 3 circuits, main circuit test-factor
module factor (
  input  [31:0] intervalo_j,
  input  [31:0] numero_x,
  input  [31:0] intervalo_i,
  input  clk,
  input  start,
  output not_found,
  output found,
  output [31:0] f_resultado
);

  wire or_1_out, or_2_out;
  wire [31:0] adder_1_out, divider_1_rem, multiplexer_1_out;

  // Probe on intervalo_j
  // Probe on numero_x
  // Probe on intervalo_i
  Multiplexer #(.width(32), .disabled(0), .enable("false")) multiplexer_1 (
    .in0(adder_1_out), .in1(intervalo_i), .out(multiplexer_1_out), .sel(start));
  // Probe on f_resultado
  Divider #(.width(32)) divider_1 (.a(numero_x), .b(f_resultado), .rem(divider_1_rem));  // open: out, upper
  Comparator #(.width(32)) comparator_1 (.a(f_resultado), .b(intervalo_j), .gt(not_found));  // open: eq, lt
  Register #(.width(32), .trigger("falling")) RegK (
    .D(multiplexer_1_out), .en(or_1_out), .Q(f_resultado), .clk(clk));  // open: clr
  or or_1 (or_1_out, start, or_2_out);
  Comparator #(.width(32)) comparator_2 (.a({32{1'b0}}), .b(divider_1_rem), .eq(found));  // open: gt, lt
  Adder #(.width(32)) adder_1 (.a(f_resultado), .b(32'h1), .out(adder_1_out));  // open: cin, cout
  or or_2 (or_2_out, not_found, ~found);  // OR_Gate

  // Notes on the sheet:
  //   Siempre:
  //   found = x%RegK==0
  //   not found = RegK>j
  //   En el pulso de bajada del reloj:
  //    if (start || !(found || not_found))
  //   RegK = start ? i : RegK+1;
endmodule

module test_factor (
);

  wire clock_1_out, factor_1_found, factor_1_not_found, tester_1_clk_out, tester_1_fail, tester_1_start,
       tester_1_success;
  wire [31:0] factor_1_f_resultado, tester_1_i, tester_1_j, tester_1_x;

  // Probe on tester_1_x
  // Probe on tester_1_i
  // Probe on tester_1_j
  Clock clock_1 (.out(clock_1_out));
  LED led_1 (.in(tester_1_fail));
  LED led_2 (.in(tester_1_success));
  factor factor_1 (
    .numero_x(tester_1_x), .intervalo_i(tester_1_i), .clk(tester_1_clk_out), .start(tester_1_start),
    .f_resultado(factor_1_f_resultado), .not_found(factor_1_not_found), .found(factor_1_found),
    .intervalo_j(tester_1_j));
  tester tester_1 (
    .found(factor_1_found), .not_found(factor_1_not_found), .f(factor_1_f_resultado), .clk_in(clock_1_out),
    .i(tester_1_i), .j(tester_1_j), .x(tester_1_x), .success(tester_1_success), .start(tester_1_start),
    .fail(tester_1_fail), .clk_out(tester_1_clk_out));
  // Probe on factor_1_f_resultado

  // Notes on the sheet:
  //   Red means failure,
  //   the output bar is
  //   inconsistent with the
  //   timing diagram for
  //   Green means success
  //   Your solution matches
  //   the full timing diagram
  //   Congratulations!
endmodule

module tester (
  input  found,
  input  not_found,
  input  [31:0] f,
  input  clk_in,
  output [31:0] j,
  output [31:0] i,
  output [31:0] x,
  output success,
  output start,
  output fail,
  output clk_out
);

  wire and_1_out, and_2_out, and_3_out, and_4_out, comparator_1_eq, d_ff_1_qn, or_1_out;
  wire [4:0] counter_1_q;
  wire [15:0] bit_extender_1_out, bit_extender_2_out;
  wire [31:0] rom_1_data, rom_2_data;

  D_Flip_Flop #(.trigger("falling")) d_ff_1 (.clk(clk_in), .D(1'b1), .Qn(d_ff_1_qn));  // open: Q, preset, en, reset
  or or_1 (or_1_out, d_ff_1_qn, found, not_found, start);
  Pull_Resistor pull_resistor_1 (.node(found));
  Pull_Resistor pull_resistor_2 (.node(not_found));
  Counter #(.width(5), .max('h1f), .trigger("falling")) counter_1 (
    .count(and_1_out), .Q(counter_1_q), .clk(clk_in));  // open: load, D, carry, clr
  and and_1 (and_1_out, or_1_out, ~fail, ~success);  // AND_Gate
  Pull_Resistor pull_resistor_3 (.node(f));
  ROM #(.addrWidth(5), .dataWidth(32)) rom_1 (
    .addr(counter_1_q), .data({rom_1_data[31:17], success, rom_1_data[15:9], start, rom_1_data[7:0]}));  // open: sel
  assign bit_extender_1_out = {{8{1'b0}}, rom_1_data[31:24]};  // Bit_Extender bit_extender_1
  Bit_Extender #(.in_width(32)) bit_extender_2 (.in(f), .out(bit_extender_2_out));
  Comparator #(.width(16)) comparator_1 (
    .a(bit_extender_1_out), .b(bit_extender_2_out), .eq(comparator_1_eq));  // open: gt, lt
  ROM #(.addrWidth(4), .dataWidth(32)) rom_2 (.addr(rom_1_data[3:0]), .data(rom_2_data));  // open: sel
  and and_2 (and_2_out, ~rom_1_data[12], rom_1_data[4], found);  // AND_Gate
  and and_3 (and_3_out, rom_1_data[12], rom_1_data[4], not_found);
  and and_4 (and_4_out, found, rom_1_data[4], rom_1_data[12], ~comparator_1_eq);  // AND_Gate
  or or_2 (fail, and_2_out, and_3_out, and_4_out);
  assign j = {{24{1'b0}}, rom_2_data[7:0]};  // Bit_Extender bit_extender_3
  assign i = {{24{1'b0}}, rom_2_data[15:8]};  // Bit_Extender bit_extender_4
  assign x = {{16{1'b0}}, rom_2_data[31:16]};  // Bit_Extender bit_extender_5
  and and_5 (clk_out, ~fail, clk_in);  // AND_Gate

  // Notes on the sheet:
  //   f-ref[31:24] success[16] found-ref[12] start[8]  valid[4] ex[1-0] 
  //   contents of rom_1 (hex, n*v repeats v):
  //   0 100 10 101 3001011 3001011 3001011 102 12 103 7001013 7001013 7001013 104 14 14 105 29001015 106
  //   fb001016 fb001016 fb011016
  //   f-ref
  //   success
  //   found-ref
  //   contents of rom_2 (hex, n*v repeats v):
  //   50303 90305 110305 4d0309 170305 e412333 f619f1ff
  //   valid
endmodule
